// Logisim project project.circ as structural Verilog: 7 circuits, main circuit main
module main (
  input  in_1,
  input  in_2,
  input  in_3,
  input  in_4,
  input  in_5,
  input  in_6,
  output out_7,
  output out_8,
  output out_9,
  output out_10
);

  wire half_adder_1_out_4, half_adder_2_out_4, half_adder_3_out_4, xor_1_out, xor_2_out, xor_3_out, xor_4_out;

  xor xor_1 (xor_1_out, in_3, in_6);
  xor xor_2 (xor_2_out, in_1, in_6);
  xor xor_3 (xor_3_out, in_5, in_6);
  xor xor_4 (xor_4_out, in_4, in_6);
  Half_Adder half_adder_1 (.in_1(in_2), .in_2(xor_2_out), .out_3(out_7), .out_4(half_adder_1_out_4));
  Half_Adder half_adder_2 (.in_1(half_adder_1_out_4), .in_2(xor_1_out), .out_3(out_8), .out_4(half_adder_2_out_4));
  Half_Adder half_adder_3 (.in_1(half_adder_2_out_4), .in_2(xor_4_out), .out_3(out_9), .out_4(half_adder_3_out_4));
  Half_Adder half_adder_4 (.in_1(half_adder_3_out_4), .in_2(xor_3_out), .out_3(out_10));  // open: out_4
endmodule

module Half_Adder (
  input  in_1,
  input  in_2,
  output out_3,
  output out_4
);

  xor xor_1 (out_3, in_1, in_2);
  and and_1 (out_4, in_2, in_1);
endmodule

module _4_Bit_Inverter (
  input  in_1,
  input  in_2,
  input  in_3,
  input  in_4,
  input  in_5,
  output out_6,
  output out_7,
  output out_8,
  output out_9,
  output out_10
);

  wire half_adder_1_out_4, half_adder_2_out_4, half_adder_3_out_4, xor_1_out, xor_2_out, xor_3_out, xor_4_out;

  xor xor_1 (xor_1_out, in_2, in_5);
  xor xor_2 (xor_2_out, in_1, in_5);
  xor xor_3 (xor_3_out, in_4, in_5);
  xor xor_4 (xor_4_out, in_3, in_5);
  Half_Adder half_adder_1 (.in_1(in_5), .in_2(xor_2_out), .out_3(out_6), .out_4(half_adder_1_out_4));
  Half_Adder half_adder_2 (.in_1(half_adder_1_out_4), .in_2(xor_1_out), .out_3(out_7), .out_4(half_adder_2_out_4));
  Half_Adder half_adder_3 (.in_1(half_adder_2_out_4), .in_2(xor_4_out), .out_3(out_8), .out_4(half_adder_3_out_4));
  Full_Adder full_adder_1 (.in_1(half_adder_3_out_4), .in_2(xor_3_out), .in_3(in_5), .out_4(out_9), .out_5(out_10));
endmodule

module _8_Bit_inverter (
  input  in_1,
  input  in_2,
  input  in_3,
  input  in_4,
  input  in_5,
  input  in_6,
  input  in_7,
  input  in_8,
  input  in_9,
  output out_10,
  output out_11,
  output out_12,
  output out_13,
  output out_14,
  output out_15,
  output out_16,
  output out_17,
  output out_18
);

  wire half_adder_1_out_4, half_adder_2_out_4, half_adder_3_out_4, half_adder_4_out_4, half_adder_5_out_4,
       half_adder_6_out_4, half_adder_7_out_4, xor_1_out, xor_2_out, xor_3_out, xor_4_out, xor_5_out,
       xor_6_out, xor_7_out, xor_8_out;

  xor xor_1 (xor_1_out, in_2, in_9);
  xor xor_2 (xor_2_out, in_6, in_9);
  xor xor_3 (xor_3_out, in_1, in_9);
  xor xor_4 (xor_4_out, in_4, in_9);
  xor xor_5 (xor_5_out, in_5, in_9);
  xor xor_6 (xor_6_out, in_8, in_9);
  xor xor_7 (xor_7_out, in_3, in_9);
  xor xor_8 (xor_8_out, in_7, in_9);
  Half_Adder half_adder_1 (.in_1(in_9), .in_2(xor_3_out), .out_3(out_10), .out_4(half_adder_1_out_4));
  Half_Adder half_adder_2 (.in_1(half_adder_1_out_4), .in_2(xor_1_out), .out_3(out_11), .out_4(half_adder_2_out_4));
  Half_Adder half_adder_3 (.in_1(half_adder_2_out_4), .in_2(xor_7_out), .out_3(out_12), .out_4(half_adder_3_out_4));
  Half_Adder half_adder_4 (.in_1(half_adder_3_out_4), .in_2(xor_4_out), .out_3(out_13), .out_4(half_adder_4_out_4));
  Half_Adder half_adder_5 (.in_1(half_adder_4_out_4), .in_2(xor_5_out), .out_3(out_14), .out_4(half_adder_5_out_4));
  Half_Adder half_adder_6 (.in_1(half_adder_5_out_4), .in_2(xor_2_out), .out_3(out_15), .out_4(half_adder_6_out_4));
  Half_Adder half_adder_7 (.in_1(half_adder_6_out_4), .in_2(xor_8_out), .out_3(out_16), .out_4(half_adder_7_out_4));
  Half_Adder half_adder_8 (.in_1(half_adder_7_out_4), .in_2(xor_6_out), .out_3(out_17), .out_4(out_18));
endmodule

module Multiplier (
  input  A3,
  input  A2,
  input  A1,
  input  A0,
  input  B3,
  input  B2,
  input  B1,
  input  B0,
  output out_9,
  output out_10,
  output out_11,
  output out_12,
  output out_13,
  output out_14,
  output out_15,
  output out_16
);

  wire b0a1_out, b0a2_out, b0a3_out, b1a0_out, b1a1_out, b1a2_out, b1a3_out, b2a0_out, b2a1_out, b2a2_out,
       b2a3_out, b3a0_out, b3a1_out, b3a2_out, b3a3_out, FA_2_out_4, FA_2_out_5, FA_3_out_4, FA_3_out_5,
       FA_4_out_4, FA_4_out_5, FA_5_out_4, FA_5_out_5, FA_out_4, FA_out_5, full_adder_2_out_5,
       full_adder_3_out_5, HA_2_out_4, HA_3_out_4, HA_4_out_4, HA_out_3, HA_out_4;

  and b3a3 (b3a3_out, B3, A3);
  and b3a2 (b3a2_out, A2, B3);
  and b3a1 (b3a1_out, B3, A1);
  and b3a0 (b3a0_out, B3, A0);
  and b2a3 (b2a3_out, A3, B2);
  and b2a1 (b2a1_out, B2, A1);
  and b2a2 (b2a2_out, A2, B2);
  Full_Adder full_adder_1 (.in_1(full_adder_2_out_5), .in_2(FA_out_5), .in_3(b3a3_out), .out_4(out_12), .out_5(out_11));
  and b2a0 (b2a0_out, B2, A0);
  Full_Adder FA (.in_1(FA_2_out_5), .in_2(b2a3_out), .in_3(HA_out_4), .out_4(FA_out_4), .out_5(FA_out_5));
  and b1a3 (b1a3_out, A3, B1);
  Half_Adder HA (.in_1(FA_3_out_5), .in_2(b1a3_out), .out_3(HA_out_3), .out_4(HA_out_4));
  Full_Adder full_adder_2 (
    .in_1(full_adder_3_out_5), .in_2(b3a2_out), .in_3(FA_out_4), .out_4(out_13), .out_5(full_adder_2_out_5));
  and b1a1 (b1a1_out, A1, B1);
  and b1a2 (b1a2_out, A2, B1);
  Full_Adder FA_2 (.in_1(FA_4_out_5), .in_2(HA_out_3), .in_3(b2a2_out), .out_4(FA_2_out_4), .out_5(FA_2_out_5));
  Full_Adder full_adder_3 (
    .in_1(HA_2_out_4), .in_2(FA_2_out_4), .in_3(b3a1_out), .out_4(out_16), .out_5(full_adder_3_out_5));
  and b1a0 (b1a0_out, B1, A0);
  Full_Adder FA_3 (.in_1(FA_5_out_5), .in_2(b1a2_out), .in_3(b0a3_out), .out_4(FA_3_out_4), .out_5(FA_3_out_5));
  Half_Adder HA_2 (.in_1(FA_4_out_4), .in_2(b3a0_out), .out_3(out_14), .out_4(HA_2_out_4));
  and b0a3 (b0a3_out, A3, B0);
  Full_Adder FA_4 (.in_1(HA_3_out_4), .in_2(b2a1_out), .in_3(FA_3_out_4), .out_4(FA_4_out_4), .out_5(FA_4_out_5));
  and b0a1 (b0a1_out, A1, B0);
  and b0a2 (b0a2_out, A2, B0);
  Full_Adder FA_5 (.in_1(HA_4_out_4), .in_2(b0a2_out), .in_3(b1a1_out), .out_4(FA_5_out_4), .out_5(FA_5_out_5));
  Half_Adder HA_3 (.in_1(FA_5_out_4), .in_2(b2a0_out), .out_3(out_9), .out_4(HA_3_out_4));
  and b0a0 (out_15, A0, B0);
  Half_Adder HA_4 (.in_1(b0a1_out), .in_2(b1a0_out), .out_3(out_10), .out_4(HA_4_out_4));
endmodule

module Full_Adder (
  input  in_1,
  input  in_2,
  input  in_3,
  output out_4,
  output out_5
);

  wire and_1_out, and_2_out, xor_1_out;

  xor xor_1 (xor_1_out, in_1, in_2);
  and and_1 (and_1_out, xor_1_out, in_3);
  and and_2 (and_2_out, in_1, in_2);
  xor xor_2 (out_4, xor_1_out, in_3);
  or or_1 (out_5, and_1_out, and_2_out);
endmodule

module _4_Bit_2s_complement_multiplier (
  input  in_1,
  input  in_2,
  input  in_3,
  input  in_4,
  input  in_5,
  input  in_6,
  input  in_7,
  input  in_8,
  input  in_9,
  input  in_10,
  output out_11,
  output out_12,
  output out_13,
  output out_14,
  output out_15,
  output out_16,
  output out_17,
  output out_18,
  output out_19
);

  wire multiplier_1_out_9, multiplier_1_out_10, multiplier_1_out_11, multiplier_1_out_12,
       multiplier_1_out_13, multiplier_1_out_14, multiplier_1_out_15, multiplier_1_out_16,
       n4_bit_inverter_1_out_6, n4_bit_inverter_1_out_7, n4_bit_inverter_1_out_8, n4_bit_inverter_1_out_9,
       n4_bit_inverter_1_out_10, n4_bit_inverter_2_out_6, n4_bit_inverter_2_out_7, n4_bit_inverter_2_out_8,
       n4_bit_inverter_2_out_9, n4_bit_inverter_2_out_10, xor_1_out;

  xor xor_1 (xor_1_out, n4_bit_inverter_1_out_10, n4_bit_inverter_2_out_10);
  _4_Bit_Inverter u_4_bit_inverter_1 (
    .in_1(in_5), .in_2(in_4), .in_3(in_3), .in_4(in_1), .in_5(in_9), .out_6(n4_bit_inverter_1_out_6),
    .out_7(n4_bit_inverter_1_out_7), .out_8(n4_bit_inverter_1_out_8), .out_9(n4_bit_inverter_1_out_9),
    .out_10(n4_bit_inverter_1_out_10));
  _8_Bit_inverter u_8_bit_inverter_1 (
    .in_1(multiplier_1_out_15), .in_2(multiplier_1_out_10), .in_3(multiplier_1_out_9),
    .in_4(multiplier_1_out_14), .in_5(multiplier_1_out_16), .in_6(multiplier_1_out_13),
    .in_7(multiplier_1_out_12), .in_8(multiplier_1_out_11), .in_9(xor_1_out), .out_10(out_19),
    .out_11(out_18), .out_12(out_17), .out_13(out_16), .out_14(out_15), .out_15(out_14), .out_16(out_13),
    .out_17(out_12), .out_18(out_11));
  Multiplier multiplier_1 (
    .A3(n4_bit_inverter_2_out_9), .A2(n4_bit_inverter_2_out_8), .A1(n4_bit_inverter_2_out_7),
    .A0(n4_bit_inverter_2_out_6), .B3(n4_bit_inverter_1_out_9), .B2(n4_bit_inverter_1_out_8),
    .B1(n4_bit_inverter_1_out_7), .B0(n4_bit_inverter_1_out_6), .out_11(multiplier_1_out_11),
    .out_12(multiplier_1_out_12), .out_13(multiplier_1_out_13), .out_16(multiplier_1_out_16),
    .out_14(multiplier_1_out_14), .out_9(multiplier_1_out_9), .out_10(multiplier_1_out_10),
    .out_15(multiplier_1_out_15));
  _4_Bit_Inverter u_4_bit_inverter_2 (
    .in_1(in_8), .in_2(in_7), .in_3(in_6), .in_4(in_2), .in_5(in_10), .out_6(n4_bit_inverter_2_out_6),
    .out_7(n4_bit_inverter_2_out_7), .out_8(n4_bit_inverter_2_out_8), .out_9(n4_bit_inverter_2_out_9),
    .out_10(n4_bit_inverter_2_out_10));
endmodule
